# Fritzing sketch SmartGas (saved by Fritzing 0.9.3b)

parts:
  MQ2 = MQ-4
  Buzzer = Passive Buzzer
  LED = RGB LED (com. cathode, rgb) [package="5 mm [THT]"]
  U1 = ESP32S-HiLetgo [part_number=ESP32S-HiLetgo]

nets:
  VCC: MQ2.VCC, U1.VIN
  GND: MQ2.GND, Buzzer.GND, LED.common_cathode, U1.GND
  N1: MQ2.AO, U1.GPIO36
  N2: Buzzer.S, U1.GPIO5
  N3: Buzzer.NC, U1.3.3
  N4: LED.red_anode, U1.GPIO4
  N5: LED.green_anode, U1.GPIO0
  N6: LED.blue_anode, U1.GPIO2

notes:
  Acá va el buzzer pero no tiene esquematico

custom parts:
  ESP32S-HiLetgo: HiLetgo ESP-WROOM-32 ESP32 ESP-32S Development Board 2.4GHz Dual-Mode WiFi + Bluetooth Dual Cores Microcontroller The ESP32 integrated with Antenna switches, RF Balun, power amplifiers, low-noise amplifiers, filters, and management modules, and the entire solution occupies the least area of PCB. 2.4 GHz Wi-Fi plus Bluetooth dual-mode chip, with TSMC Ultra-low power consumption 40nm technology,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
